# Fritzing sketch board-schematic (saved by Fritzing 0.9.10b)
breadboards: 1

parts:
  MCU1 = Raspberry Pi Zero
  Mod1 = Amica NodeMCU DEVKIT 1.0

nets:
  N1: MCU1.pin_1, MCU1.pin_17, Mod1.pin_30
  N2: MCU1.pin_15, Mod1.pin_20
  N3: MCU1.pin_19, Mod1.pin_21
  N4: MCU1.pin_20, MCU1.pin_25, Mod1.pin2, Mod1.pin_29
  N5: MCU1.pin_23, Mod1.pin_24
  N6: MCU1.pin_24, Mod1.pin_22
